// Logisim project hack.circ as structural Verilog: 4 circuits, main circuit main
module main (
);

  wire clock_1_out, clock_2_out, cpu_1_writem, not_1_out, not_2_out;
  wire [14:0] cpu_1_addr, cpu_1_pc;
  wire [15:0] controlled_buffer_2_out, cpu_1_outm, ram_1_data, rom_1_data;

  ROM #(.addrWidth(15), .dataWidth(16)) rom_1 (.addr(cpu_1_pc), .data(rom_1_data));  // open: sel
  Clock clock_1 (.out(clock_1_out));
  CPU cpu_1 (
    .inM(controlled_buffer_2_out), .inst(rom_1_data), .CLK(clock_1_out), .PC(cpu_1_pc), .addr(cpu_1_addr),
    .outM(cpu_1_outm), .writeM(cpu_1_writem));  // open: RESET
  // Probe on cpu_1_pc
  Clock clock_2 (.out(clock_2_out));
  RAM #(.addrWidth(15), .dataWidth(16)) ram_1 (
    .addr(cpu_1_addr), .data(ram_1_data), .clk(clock_2_out), .ld(not_1_out));  // open: sel, clr
  not not_1 (not_1_out, cpu_1_writem);
  assign ram_1_data = cpu_1_writem ? cpu_1_outm : 16'bz;  // Controlled_Buffer controlled_buffer_1
  assign controlled_buffer_2_out = not_2_out ? ram_1_data : 16'bz;  // Controlled_Buffer controlled_buffer_2
  not not_2 (not_2_out, cpu_1_writem);
endmodule

module ALU (
  input  zx,
  input  nx,
  input  zy,
  input  ny,
  input  add,
  input  no,
  input  [15:0] x,
  input  [15:0] y,
  output [15:0] out,
  output zero,
  output neg
);

  wire not_1_out, pull_resistor_1_node;
  wire [15:0] adder_1_out, and_1_out, condnegator_1_out, condnegator_2_out, multiplexer_1_out,
       multiplexer_2_out, multiplexer_3_out;

  Multiplexer #(.width(16), .enable("false")) multiplexer_1 (
    .in0(x), .in1({16{1'b0}}), .out(multiplexer_1_out), .sel(zx));
  CondNegator condnegator_1 (.in(multiplexer_1_out), .neg(nx), .out(condnegator_1_out));
  Multiplexer #(.width(16), .enable("false")) multiplexer_2 (
    .in0(y), .in1({16{1'b0}}), .out(multiplexer_2_out), .sel(zy));
  CondNegator condnegator_2 (.in(multiplexer_2_out), .neg(ny), .out(condnegator_2_out));
  Pull_Resistor pull_resistor_1 (.node(pull_resistor_1_node));
  Adder #(.width(16)) adder_1 (
    .a(condnegator_1_out), .b(condnegator_2_out), .out(adder_1_out), .cin(pull_resistor_1_node));  // open: cout
  assign and_1_out = condnegator_1_out & condnegator_2_out;  // AND_Gate and_1, 16 bits wide
  not not_1 (not_1_out, add);
  Multiplexer #(.width(16), .enable("false")) multiplexer_3 (
    .in0(adder_1_out), .in1(and_1_out), .out(multiplexer_3_out), .sel(not_1_out));
  CondNegator condnegator_3 (.in(multiplexer_3_out), .neg(no), .out(out));
  Comparator #(.width(16)) comparator_1 (.a(out), .b({16{1'b0}}), .eq(zero), .lt(neg));  // open: gt
endmodule

// ±x
module CondNegator (
  input  neg,
  input  [15:0] in,
  output [15:0] out
);

  wire [15:0] negator_1_out;

  Negator #(.width(16)) negator_1 (.in(in), .out(negator_1_out));
  Multiplexer #(.width(16), .enable("false")) multiplexer_1 (.in0(in), .in1(negator_1_out), .out(out), .sel(neg));
endmodule

module CPU (
  input  [15:0] inM,
  input  [15:0] inst,
  input  CLK,
  input  RESET,
  output [14:0] PC,
  output [14:0] addr,
  output [15:0] outM,
  output writeM
);

  wire and_1_out, and_2_out, and_3_out, and_4_out, Jump, Neg, nor_1_out, not_1_out, or_1_out, or_2_out, Zero;
  wire [15:0] D_q, multiplexer_1_out, multiplexer_2_out;
  wire [15:15] A_q, pull_resistor_1_node;

  Pull_Resistor #(.pull(1)) pull_resistor_1 (.node(pull_resistor_1_node[15]));
  Multiplexer #(.width(16), .enable("false")) multiplexer_1 (
    .in0({pull_resistor_1_node[15], inst[14:0]}), .in1(outM), .out(multiplexer_1_out), .sel(inst[15]));
  or or_1 (or_1_out, ~inst[15], inst[3]);  // OR_Gate
  and and_1 (and_1_out, inst[15], inst[4]);
  Register #(.width(16)) A (.D(multiplexer_1_out), .en(or_1_out), .Q({A_q[15], addr}), .clk(CLK), .clr(RESET));
  Register #(.width(16)) D (.D(outM), .en(and_1_out), .Q(D_q), .clk(CLK), .clr(RESET));
  Multiplexer #(.width(16), .enable("false")) multiplexer_2 (
    .in0({A_q[15], addr}), .in1(inM), .out(multiplexer_2_out), .sel(inst[12]));
  Counter #(.width(15), .max('h7fff)) u_PC (
    .load(Jump), .D(addr), .count(not_1_out), .Q(PC), .clk(CLK), .clr(RESET));  // open: carry
  not not_1 (not_1_out, Jump);
  ALU alu_1 (
    .x(multiplexer_2_out), .y(D_q), .zx(inst[6]), .nx(inst[7]), .zy(inst[8]), .ny(inst[9]), .add(inst[10]),
    .no(inst[11]), .zero(Zero), .neg(Neg), .out(outM));
  and and_2 (and_2_out, Neg, inst[0]);
  and and_3 (and_3_out, Zero, inst[1]);
  nor nor_1 (nor_1_out, Zero, Neg);
  and and_4 (and_4_out, nor_1_out, inst[2]);
  or or_2 (or_2_out, and_2_out, and_3_out, and_4_out);
  and and_5 (Jump, or_2_out, inst[15]);

  assign writeM = inst[5];

  // Other names for the same wires on the sheet: _0 = inst[0]; j[2:0] = inst[2:0]; v[14:0] = inst[14:0];
  //   _0_t = inst[1]; _0_t_t = inst[2]; d[2:0] = inst[5:3]; WA = inst[3]; WD = inst[4]; c[5:0] = inst[11:6];
  //   a = inst[12]; Arith = inst[15]; Result[15:0] = outM

  // Notes on the sheet:
  //   Instruction decoder
endmodule
